# Fritzing sketch Untitled Sketch (saved by Fritzing 0.9.1b)
breadboards: 1

parts:
  Part1 = Arduino Uno (Rev3) - ICSP
  LCD1 = LCD screen
  RE1 = Rotary Encoder [package=THT]
  LED1 = LED - 5mm [color="Red (633nm)" package="5 mm [THT]"]
  LED2 = LED - 5mm [color="Red (633nm)" package="5 mm [THT]"]
  LED3 = LED - 5mm [color="Red (633nm)" package="5 mm [THT]"]
  LED4 = LED - 5mm [color="Red (633nm)" package="5 mm [THT]"]
  R1 = Resistor [tolerance=±5% resistance=220 package=THT]
  R2 = Resistor [tolerance=±5% resistance=220 package=THT]
  R3 = Resistor [tolerance=±5% resistance=220 package=THT]
  R4 = Resistor [tolerance=±5% resistance=220 package=THT]
  S1 = Pushbutton [package="[THT]"]
  S2 = Pushbutton [package="[THT]"]
  S3 = Pushbutton [package="[THT]"]
  S4 = Pushbutton [package="[THT]"]
  R5 = Resistor [tolerance=±5% resistance=220 package=THT]
  R6 = Resistor [tolerance=±5% resistance=220 package=THT]
  R7 = Resistor [tolerance=±5% resistance=220 package=THT]
  R8 = Resistor [tolerance=±5% resistance=220 package=THT]

nets:
  5V: Part1.5V, LCD1.VDD, LCD1.LED+, RE1.EncoderPinB, S1.Pin_3, S1.Pin_4, S2.Pin_3, S2.Pin_4, S3.Pin_3, S3.Pin_4, S4.Pin_3, S4.Pin_4
  N1: Part1.D8, R1.Pin_1
  N2: Part1.D9_PWM, R2.Pin_1
  N3: Part1.D10_PWM/SS, R4.Pin_1
  N4: Part1.D11_PWM/MOSI, S3.Pin_1, S3.Pin_2, R7.Pin_1
  N5: Part1.D12/MISO, R3.Pin_1
  N6: Part1.D13/SCK, S4.Pin_1, S4.Pin_2, R8.Pin_1
  N7: Part1.D0/RX, LCD1.E
  N8: Part1.D1/TX, LCD1.RS
  N9: Part1.D2, LCD1.DB7
  N10: Part1.D3_PWM, LCD1.DB6
  N11: Part1.D4, LCD1.DB5
  N12: Part1.D5_PWM, LCD1.DB4
  N13: Part1.D6_PWM, S1.Pin_1, S1.Pin_2, R5.Pin_1
  N14: Part1.D7, S2.Pin_1, S2.Pin_2, R6.Pin_1
  GND: Part1.GND, LCD1.VSS, LCD1.R/W, LCD1.LED-, RE1.EncoderPinA, LED1.cathode, LED2.cathode, LED3.cathode, LED4.cathode, R5.Pin_0, R7.Pin_0
  N15: LCD1.V0, RE1.EncoderPinC
  N16: LED1.anode, R1.Pin_0
  N17: LED2.anode, R2.Pin_0
  N18: LED3.anode, R4.Pin_0
  N19: LED4.anode, R3.Pin_0
